// Logisim project 2sCompliment.circ as structural Verilog: 1 circuit, main circuit main
module main (
  input  _1,
  input  _0,
  input  B0,
  input  B1,
  input  B2,
  input  B3,
  output Cout,
  output B0_2,
  output B1_2,
  output B2_2,
  output B3_2
);

  wire not_1_out, not_2_out, not_3_out, not_4_out;

  _4bitAdder_main main_1 (
    .Cin0(_0), .Cout(Cout), .S0(B0_2), .S1(B1_2), .S2(B2_2), .S3(B3_2), .A0(not_1_out), .A1(not_4_out),
    .A2(not_2_out), .A3(not_3_out), .B0(_0), .B1(_0), .B2(_0), .B3(_1));
  not not_1 (not_1_out, B0);
  not not_2 (not_2_out, B2);
  not not_3 (not_3_out, B3);
  not not_4 (not_4_out, B1);
endmodule
