// Logisim project 4bitAdder.circ as structural Verilog: 1 circuit, main circuit main
module main (
  input  Cin0,
  input  A0,
  input  A1,
  input  A2,
  input  A3,
  input  B0,
  input  B1,
  input  B2,
  input  B3,
  output Cout,
  output S0,
  output S1,
  output S2,
  output S3
);

  wire main_2_cout, main_3_cout, main_4_cout;

  FullAdder_main main_1 (.A(A0), .B(B0), .Cin(main_3_cout), .S(S0), .Cout(Cout));
  FullAdder_main main_2 (.A(A2), .B(B2), .Cin(main_4_cout), .S(S2), .Cout(main_2_cout));
  FullAdder_main main_3 (.A(A1), .B(B1), .Cin(main_2_cout), .S(S1), .Cout(main_3_cout));
  FullAdder_main main_4 (.A(A3), .B(B3), .Cin(Cin0), .S(S3), .Cout(main_4_cout));
endmodule
