// Logisim project 4bitDecrement.circ as structural Verilog: 1 circuit, main circuit main
module main (
  input  _1,
  input  _0,
  input  A0,
  input  A1,
  input  A2,
  input  A3,
  output Cout,
  output S0,
  output S1,
  output S2,
  output S3
);

  _4bitSubtractor_main main_1 (
    ._1(_1), ._0(_0), .Cout(Cout), .S0(S0), .S1(S1), .S2(S2), .S3(S3), .A0(A0), .A1(A1), .A2(A2), .A3(A3),
    .B0(_0), .B1(_0), .B2(_0), .B3(_1));
endmodule
