// Logisim project 4bitSubtractor.circ as structural Verilog: 1 circuit, main circuit main
module main (
  input  A0,
  input  A1,
  input  A2,
  input  A3,
  input  _1,
  input  _0,
  input  B0,
  input  B1,
  input  B2,
  input  B3,
  output Cout,
  output S0,
  output S1,
  output S2,
  output S3
);

  wire _2_s_Compliment_b0_2, _2_s_Compliment_b1_2, _2_s_Compliment_b2_2, _2_s_Compliment_b3_2,
       _2_s_Compliment_cout, Adder_cout;

  not not_1 (Cout, Adder_cout);
  _4bitAdder_main Adder (
    .Cin0(_2_s_Compliment_cout), .Cout(Adder_cout), .S0(S0), .S1(S1), .S2(S2), .S3(S3), .A0(A0), .A1(A1),
    .A2(A2), .A3(A3), .B0(_2_s_Compliment_b0_2), .B1(_2_s_Compliment_b1_2), .B2(_2_s_Compliment_b2_2),
    .B3(_2_s_Compliment_b3_2));
  _2sCompliment_main _2_s_Compliment (
    ._1(_1), ._0(_0), .Cout(_2_s_Compliment_cout), .B0_2(_2_s_Compliment_b0_2), .B1_2(_2_s_Compliment_b1_2),
    .B2_2(_2_s_Compliment_b2_2), .B3_2(_2_s_Compliment_b3_2), .B0(B0), .B1(B1), .B2(B2), .B3(B3));
endmodule
