// Logisim project ALU.circ as structural Verilog: 1 circuit, main circuit main
module main (
  input  b,
  input  a,
  input  A0,
  input  A1,
  input  A2,
  input  A3,
  input  B0,
  input  B1,
  input  B2,
  input  B3,
  output Cout,
  output S0,
  output S1,
  output S2,
  output S3
);

  wire main_1_cout, main_1_s0, main_1_s1, main_1_s2, main_1_s3, main_2_deca0, main_2_deca1, main_2_deca2,
       main_2_deca3, main_2_inca0, main_2_inca1, main_2_inca2, main_2_inca3, main_2_subtracta0,
       main_2_subtracta1, main_2_subtracta2, main_2_subtracta3, main_2_subtractb0, main_2_subtractb1,
       main_2_subtractb2, main_2_subtractb3, main_2_suma0, main_2_suma1, main_2_suma2, main_2_suma3,
       main_2_sumb0, main_2_sumb1, main_2_sumb2, main_2_sumb3, main_4_cout, main_4_s0, main_4_s1, main_4_s2,
       main_4_s3, main_5_cout, main_5_s0, main_5_s1, main_5_s2, main_5_s3, main_6_cout, main_6_s0, main_6_s1,
       main_6_s2, main_6_s3;

  _4bitAdder_main main_1 (
    .Cin0(1'b0), .Cout(main_1_cout), .S0(main_1_s0), .S1(main_1_s1), .S2(main_1_s2), .S3(main_1_s3),
    .A0(main_2_suma0), .A1(main_2_suma1), .A2(main_2_suma2), .A3(main_2_suma3), .B0(main_2_sumb0),
    .B1(main_2_sumb1), .B2(main_2_sumb2), .B3(main_2_sumb3));
  DEMUXFull_main main_2 (
    .b(b), .a(a), .SumA0(main_2_suma0), .SumA1(main_2_suma1), .SumA2(main_2_suma2), .SumA3(main_2_suma3),
    .SumB0(main_2_sumb0), .SumB1(main_2_sumb1), .SumB2(main_2_sumb2), .SumB3(main_2_sumb3),
    .SubtractA0(main_2_subtracta0), .SubtractA1(main_2_subtracta1), .SubtractA2(main_2_subtracta2),
    .SubtractA3(main_2_subtracta3), .SubtractB0(main_2_subtractb0), .SubtractB1(main_2_subtractb1),
    .SubtractB2(main_2_subtractb2), .SubtractB3(main_2_subtractb3), .IncA0(main_2_inca0),
    .IncA1(main_2_inca1), .IncA2(main_2_inca2), .IncA3(main_2_inca3), .DecA0(main_2_deca0),
    .DecA1(main_2_deca1), .DecA2(main_2_deca2), .DecA3(main_2_deca3), .A0(A0), .A1(A1), .A2(A2), .A3(A3),
    .B0(B0), .B1(B1), .B2(B2), .B3(B3));  // open: IncB0, IncB1, IncB2, IncB3, DecB0, DecB1, DecB2, DecB3
  MUX5Bit_main main_3 (
    .Sum(main_1_cout), .Sum_2(main_1_s0), .Sum_3(main_1_s1), .Sum_4(main_1_s2), .Sum_5(main_1_s3),
    .Sub(main_4_cout), .Sub_2(main_4_s0), .Sub_3(main_4_s1), .Sub_4(main_4_s2), .Sub_5(main_4_s3),
    .Inc(main_5_cout), .Inc_2(main_5_s0), .Inc_3(main_5_s1), .Inc_4(main_5_s2), .Inc_5(main_5_s3),
    .Dec(main_6_cout), .Dec_2(main_6_s0), .Dec_3(main_6_s1), .Dec_4(main_6_s2), .Dec_5(main_6_s3), .a(a),
    .b(b), .out_23(Cout), .out_24(S0), .out_25(S1), .out_26(S2), .out_27(S3));
  _4bitSubtractor_main main_4 (
    ._1(1'b1), ._0(1'b0), .Cout(main_4_cout), .S0(main_4_s0), .S1(main_4_s1), .S2(main_4_s2), .S3(main_4_s3),
    .A0(main_2_subtracta0), .A1(main_2_subtracta1), .A2(main_2_subtracta2), .A3(main_2_subtracta3),
    .B0(main_2_subtractb0), .B1(main_2_subtractb1), .B2(main_2_subtractb2), .B3(main_2_subtractb3));
  _4bitIncrement_main main_5 (
    ._1(1'b1), ._0(1'b0), .Cout(main_5_cout), .S0(main_5_s0), .S1(main_5_s1), .S2(main_5_s2), .S3(main_5_s3),
    .A0(main_2_inca0), .A1(main_2_inca1), .A2(main_2_inca2), .A3(main_2_inca3));
  _4bitDecrement_main main_6 (
    ._1(1'b1), ._0(1'b0), .Cout(main_6_cout), .S0(main_6_s0), .S1(main_6_s1), .S2(main_6_s2), .S3(main_6_s3),
    .A0(main_2_deca0), .A1(main_2_deca1), .A2(main_2_deca2), .A3(main_2_deca3));

  // Notes on the sheet:
  //   a b op
  //   0 0 Sum
  //   0 1 Subtract
  //   1 0 Increment
  //   1 1 Decrement
  //   Sum
  //   MUX
  //   Subtract
  //   Inc
  //   DEMUX
  //   Dec
endmodule
