// Logisim project DEMUX1bit.circ as structural Verilog: 1 circuit, main circuit main
module main (
  input  a,
  input  b,
  input  Input,
  output SUM,
  output Subtract,
  output Increment,
  output Decrement,
  output a_2,
  output b_2
);

  wire not_1_out, not_2_out;

  not not_1 (not_1_out, a);
  not not_2 (not_2_out, b);
  and and_1 (SUM, not_2_out, not_1_out, Input);
  and and_2 (Subtract, not_1_out, b, Input);
  and and_3 (Increment, not_2_out, a, Input);
  and and_4 (Decrement, a, b, Input);

  assign a_2 = a;
  assign b_2 = b;
endmodule
