// Logisim project DEMUX4bit copy.circ as structural Verilog: 1 circuit, main circuit main
module main (
  input  a,
  input  b,
  input  A3,
  input  A2,
  input  A1,
  input  A0,
  output Sum3,
  output Sum2,
  output Sum1,
  output Sum0,
  output Subtract3,
  output Subtract2,
  output Subtract1,
  output Subtract0,
  output Increment3,
  output Increment2,
  output Increment1,
  output Increment0,
  output Decrement3,
  output Decrement2,
  output Decrement1,
  output Decrement0,
  output a_2,
  output b_2
);

  wire main_1_a_2, main_1_b_2, main_2_a_2, main_2_b_2, main_3_a_2, main_3_b_2;

  DEMUX1bit_main main_1 (
    .Input(A3), .a(a), .b(b), .a_2(main_1_a_2), .b_2(main_1_b_2), .SUM(Sum3), .Subtract(Subtract3),
    .Increment(Increment3), .Decrement(Decrement3));
  DEMUX1bit_main main_2 (
    .Input(A2), .a(main_1_a_2), .b(main_1_b_2), .a_2(main_2_a_2), .b_2(main_2_b_2), .SUM(Sum2),
    .Subtract(Subtract2), .Increment(Increment2), .Decrement(Decrement2));
  DEMUX1bit_main main_3 (
    .Input(A1), .a(main_2_a_2), .b(main_2_b_2), .a_2(main_3_a_2), .b_2(main_3_b_2), .SUM(Sum1),
    .Subtract(Subtract1), .Increment(Increment1), .Decrement(Decrement1));
  DEMUX1bit_main main_4 (
    .Input(A0), .a(main_3_a_2), .b(main_3_b_2), .a_2(a_2), .b_2(b_2), .SUM(Sum0), .Subtract(Subtract0),
    .Increment(Increment0), .Decrement(Decrement0));
endmodule
