// Logisim project DEMUXFull.circ as structural Verilog: 1 circuit, main circuit main
module main (
  input  b,
  input  a,
  input  A0,
  input  A1,
  input  A2,
  input  A3,
  input  B0,
  input  B1,
  input  B2,
  input  B3,
  output SumA0,
  output SumA1,
  output SumA2,
  output SumA3,
  output SumB0,
  output SumB1,
  output SumB2,
  output SumB3,
  output SubtractA0,
  output SubtractA1,
  output SubtractA2,
  output SubtractA3,
  output SubtractB0,
  output SubtractB1,
  output SubtractB2,
  output SubtractB3,
  output IncA0,
  output IncA1,
  output IncA2,
  output IncA3,
  output IncB0,
  output IncB1,
  output IncB2,
  output IncB3,
  output DecA0,
  output DecA1,
  output DecA2,
  output DecA3,
  output DecB0,
  output DecB1,
  output DecB2,
  output DecB3
);

  wire main_2_p6, main_2_p7;

  // DEMUX4bit_main main_1: pin names not known; wires that end beside it: b, a, SumA3, SumA2, SumA1, SumA0, SubtractA3, SubtractA2, SubtractA1, A3, SubtractA0, A2, IncA3, A1, IncA2, A0, IncA1
  // DEMUX4bit_main main_2: pin names not known; wires that end beside it: IncA0, DecA3, DecA2, DecA1, DecA0, main_2_p6, main_2_p7, main_2_p6, main_2_p7, SumB3, SumB2, SumB1, SumB0, SubtractB3, SubtractB2, SubtractB1, B3, SubtractB0, B2, IncB3, B1, IncB2, B0, IncB1, IncB0, DecB3, DecB2, DecB1, DecB0
endmodule
