// Logisim project MUX1bit.circ as structural Verilog: 1 circuit, main circuit main
module main (
  input  a,
  input  b,
  input  Sum,
  input  Sub,
  input  Inc,
  input  Dec,
  output out_7,
  output ao,
  output bo
);

  wire and_1_out, and_2_out, and_3_out, and_4_out, not_1_out, not_2_out;

  not not_1 (not_1_out, a);
  not not_2 (not_2_out, b);
  and and_1 (and_1_out, Sum, not_1_out, not_2_out);
  and and_2 (and_2_out, Sub, b, not_1_out);
  and and_3 (and_3_out, Inc, not_2_out, a);
  and and_4 (and_4_out, Dec, b, a);
  or or_1 (out_7, and_1_out, and_2_out, and_3_out, and_4_out);

  assign ao = a;
  assign bo = b;
endmodule
