// Logisim project MUX5Bit.circ as structural Verilog: 1 circuit, main circuit main
module main (
  input  a,
  input  b,
  input  Sum,
  input  Sum_2,
  input  Sum_3,
  input  Sum_4,
  input  Sum_5,
  input  Sub,
  input  Sub_2,
  input  Sub_3,
  input  Sub_4,
  input  Sub_5,
  input  Inc,
  input  Inc_2,
  input  Inc_3,
  input  Inc_4,
  input  Inc_5,
  input  Dec,
  input  Dec_2,
  input  Dec_3,
  input  Dec_4,
  input  Dec_5,
  output out_23,
  output out_24,
  output out_25,
  output out_26,
  output out_27
);

  wire main_1_ao, main_1_bo, main_2_ao, main_2_bo, main_3_ao, main_3_bo, main_4_ao, main_4_bo;

  MUX1bit_main main_1 (
    .Sum(Sum), .Sub(Sub), .Inc(Inc), .Dec(Dec), .a(a), .b(b), .ao(main_1_ao), .bo(main_1_bo), .out_7(out_23));
  MUX1bit_main main_2 (
    .Sum(Sum_2), .Sub(Sub_2), .Inc(Inc_2), .Dec(Dec_2), .a(main_1_ao), .b(main_1_bo), .ao(main_2_ao),
    .bo(main_2_bo), .out_7(out_24));
  MUX1bit_main main_3 (
    .Sum(Sum_3), .Sub(Sub_3), .Inc(Inc_3), .Dec(Dec_3), .a(main_2_ao), .b(main_2_bo), .ao(main_3_ao),
    .bo(main_3_bo), .out_7(out_25));
  MUX1bit_main main_4 (
    .Sum(Sum_4), .Sub(Sub_4), .Inc(Inc_4), .Dec(Dec_4), .a(main_3_ao), .b(main_3_bo), .ao(main_4_ao),
    .bo(main_4_bo), .out_7(out_26));
  MUX1bit_main main_5 (
    .Sum(Sum_5), .Sub(Sub_5), .Inc(Inc_5), .Dec(Dec_5), .a(main_4_ao), .b(main_4_bo), .out_7(out_27));  // open: ao, bo
endmodule
